// Logisim project exp6-1a.circ as structural Verilog: 1 circuit, main circuit main
module main (
  input  A,
  input  B,
  input  C,
  output F
);

  wire and_1_out, and_2_out, and_3_out, and_4_out, and_5_out, not_1_out, not_2_out, not_3_out;

  not not_1 (not_1_out, A);
  not not_2 (not_2_out, C);
  not not_3 (not_3_out, B);
  and and_1 (and_1_out, not_1_out, not_3_out, not_2_out);
  and and_2 (and_2_out, not_1_out, B, not_2_out);
  and and_3 (and_3_out, not_1_out, not_3_out, C);
  and and_4 (and_4_out, A, not_3_out, not_2_out);
  and and_5 (and_5_out, A, B, not_2_out);
  or or_1 (F, and_1_out, and_2_out, and_3_out, and_4_out, and_5_out);

  // Notes on the sheet:
  //   Stephen Allan
  //   Section: 01
  //   Experiment: 6
  //   Activity: 1a
endmodule
