// Logisim project exp6-1c.circ as structural Verilog: 1 circuit, main circuit main
module main (
  input  [2:0] A_B_C,
  output F
);

  Multiplexer #(.select(3), .width(1)) multiplexer_1 (
    .in0(1'b0), .in1(1'b1), .in2(1'b0), .in3(1'b1), .in4(1'b0), .in5(1'b1), .in6(1'b1), .in7(1'b0), .out(F),
    .sel(A_B_C));

  // Notes on the sheet:
  //   Stephen Allan
  //   Section: 01
  //   Experiment: 6
  //   Activity: 1c
endmodule
